# Fritzing sketch GyverControl_MH-Z19B_adapter (saved by Fritzing 0.9.4)
perfboards: 1

parts:
  TD-er1 = MH-Z19 CO2 sensor [part_number=MH-Z19]
  SERV2 = female pin header, 3 pins [form="♀ (female)"]
  SENS1 = male pin header, 3 pins [form="♂ (male)"]
  J1 = female pin header, 4 pins [form="♀ (female)"]
  J4 = male pin header, 4 pins [form="♂ (male)"]

nets:
  N1: TD-er1.RX, SENS1.pin2, J4.pin4
  N2: TD-er1.TX, SENS1.pin1, J4.pin3
  N3: TD-er1.Vin, SERV2.pin2, J1.pin4
  N4: TD-er1.GND, SENS1.pin3, J1.pin3
  N5: TD-er1.AOT, J1.pin2
  N6: TD-er1.PWM, J1.pin1
